// Logisim project prac.circ as structural Verilog: 1 circuit, main circuit main
module main (
  input  in_1,
  input  in_2,
  input  in_3,
  input  in_4,
  input  in_5,
  input  in_6,
  input  in_7,
  input  in_8,
  input  in_9,
  output out_10,
  output out_11,
  output out_12,
  output out_13
);

  wire and_1_out, and_2_out, clock_1_out, xor_1_out;

  Demultiplexer demultiplexer_1 ();  // open: out0, out1, in, sel, en
  S_R_Flip_Flop s_r_ff_1 ();  // open: S, clk, R, Q, Qn, preset, reset, en
  Clock clock_1 (.out(clock_1_out));
  D_Flip_Flop d_ff_1 ();  // open: clk, D, Q, Qn, preset, en, reset
  Decoder decoder_1 ();  // open: out0, out1, sel, en
  Multiplexer multiplexer_1 ();  // open: in0, in1, out, sel, en
  T_Flip_Flop t_ff_1 ();  // open: clk, T, Q, Qn, preset, reset, en
  J_K_Flip_Flop j_k_ff_1 (
    .J(in_5), .clk(clock_1_out), .K(in_6), .Q(out_12), .Qn(out_13), .preset(in_9), .en(in_7), .reset(in_8));
  // Even_Parity even_parity_1 is placed but not wired
  // Odd_Parity odd_parity_1 is placed but not wired
  xor xor_1 (xor_1_out, in_1, in_3);
  and and_1 (and_1_out, in_1, in_3);
  and and_2 (and_2_out, xor_1_out, in_4);
  xor xor_2 (out_10, xor_1_out, in_4);
  or or_1 (out_11, and_2_out, and_1_out);
endmodule
